# Fritzing sketch DualMotorDriver (saved by Fritzing 0.9.3b)
circuit board: 6.8235cm x 6.24022cm
breadboards: 1

parts:
  M1 = DC Motor
  M2 = DC Motor
  Part1 = Motor Driver 1A Dual TB6612FNG
  VCC1 = Battery block 9V
  Raspberry_Pi1 = Raspberry Pi B+

nets:
  N1: M1.pin_1, Part1.A02
  N2: M1.pin_2, Part1.A01
  N3: M2.pin_1, Part1.B01
  N4: M2.pin_2, Part1.B02
  GND: Part1.GND, VCC1.-, Raspberry_Pi1.GND
  3V3: Part1.VCC, Raspberry_Pi1.3v3, Raspberry_Pi1.3V3
  N5: Part1.VM, VCC1.+
  N6: Part1.PWMA, Raspberry_Pi1.GPIO18
  N7: Part1.AIN2, Raspberry_Pi1.GPIO24
  N8: Part1.AIN1, Raspberry_Pi1.GPIO8
  N9: Part1.STBY, Raspberry_Pi1.GPIO9
  N10: Part1.BIN1, Raspberry_Pi1.GPIO22
  N11: Part1.BIN2, Raspberry_Pi1.GPIO27
  N12: Part1.PWMB, Raspberry_Pi1.GPIO19
